// Logisim project Problem3bCircuit.circ as structural Verilog: 1 circuit, main circuit main
module main (
  input  I3,
  input  I2,
  input  I1,
  output Q1,
  output Q0
);

  wire and_1_out, not_1_out;

  not not_1 (not_1_out, I2);
  and and_1 (and_1_out, not_1_out, I1);
  or or_1 (Q1, I3, I2);
  or or_2 (Q0, I3, and_1_out);
endmodule
