// Logisim project Problem4Circuit.circ as structural Verilog: 1 circuit, main circuit main
module main (
  input  SClock,
  input  RClock,
  input  DataIn,
  output Q0,
  output Q1,
  output Q2,
  output Q3,
  output Q4,
  output Q5,
  output Q6,
  output Q7
);

  wire F0_q, F1_q, F2_q, F3_q, F4_q, F5_q, F6_q, F7_q;

  D_Flip_Flop F0 (.D(DataIn), .clk(SClock), .Q(F0_q));  // open: Qn, preset, reset
  D_Flip_Flop F1 (.D(F0_q), .clk(SClock), .Q(F1_q));  // open: Qn, preset, reset
  D_Flip_Flop F2 (.D(F1_q), .clk(SClock), .Q(F2_q));  // open: Qn, preset, reset
  D_Flip_Flop F3 (.D(F2_q), .clk(SClock), .Q(F3_q));  // open: Qn, preset, reset
  D_Flip_Flop F4 (.D(F3_q), .clk(SClock), .Q(F4_q));  // open: Qn, preset, reset
  D_Flip_Flop F5 (.D(F4_q), .clk(SClock), .Q(F5_q));  // open: Qn, preset, reset
  D_Flip_Flop F6 (.D(F5_q), .clk(SClock), .Q(F6_q));  // open: Qn, preset, reset
  D_Flip_Flop F7 (.D(F6_q), .clk(SClock), .Q(F7_q));  // open: Qn, preset, reset
  D_Flip_Flop R0 (.D(F0_q), .clk(RClock), .Q(Q0));  // open: Qn, preset, reset
  D_Flip_Flop R1 (.D(F1_q), .clk(RClock), .Q(Q1));  // open: Qn, preset, reset
  D_Flip_Flop R2 (.D(F2_q), .clk(RClock), .Q(Q2));  // open: Qn, preset, reset
  D_Flip_Flop R3 (.D(F3_q), .clk(RClock), .Q(Q3));  // open: Qn, preset, reset
  D_Flip_Flop R4 (.D(F4_q), .clk(RClock), .Q(Q4));  // open: Qn, preset, reset
  D_Flip_Flop R5 (.D(F5_q), .clk(RClock), .Q(Q5));  // open: Qn, preset, reset
  D_Flip_Flop R6 (.D(F6_q), .clk(RClock), .Q(Q6));  // open: Qn, preset, reset
  D_Flip_Flop R7 (.D(F7_q), .clk(RClock), .Q(Q7));  // open: Qn, preset, reset
endmodule
