// Logisim project demoInstructions.circ as structural Verilog: 9 circuits, main circuit AutomatedAdder
module DTypeFFx8 (
  input  [7:0] DataIn,
  input  Clock,
  input  Clear,
  output [7:0] DataOut
);

  D_Flip_Flop d_ff_1 (.D(DataIn[0]), .clk(Clock), .Q(DataOut[0]), .reset(Clear));  // open: Qn, preset
  D_Flip_Flop d_ff_2 (.D(DataIn[1]), .clk(Clock), .Q(DataOut[1]), .reset(Clear));  // open: Qn, preset
  D_Flip_Flop d_ff_3 (.D(DataIn[2]), .clk(Clock), .Q(DataOut[2]), .reset(Clear));  // open: Qn, preset
  D_Flip_Flop d_ff_4 (.D(DataIn[3]), .clk(Clock), .Q(DataOut[3]), .reset(Clear));  // open: Qn, preset
  D_Flip_Flop d_ff_5 (.D(DataIn[4]), .clk(Clock), .Q(DataOut[4]), .reset(Clear));  // open: Qn, preset
  D_Flip_Flop d_ff_6 (.D(DataIn[5]), .clk(Clock), .Q(DataOut[5]), .reset(Clear));  // open: Qn, preset
  D_Flip_Flop d_ff_7 (.D(DataIn[6]), .clk(Clock), .Q(DataOut[6]), .reset(Clear));  // open: Qn, preset
  D_Flip_Flop d_ff_8 (.D(DataIn[7]), .clk(Clock), .Q(DataOut[7]), .reset(Clear));  // open: Qn, preset
endmodule

module Counter16bit (
  input  Clock,
  input  Clear,
  output [15:0] Count
);

  wire d_ff_1_qn, d_ff_2_qn, d_ff_3_qn, d_ff_4_qn, d_ff_5_qn, d_ff_6_qn, d_ff_7_qn, d_ff_8_qn, d_ff_9_qn,
       d_ff_10_qn, d_ff_11_qn, d_ff_12_qn, d_ff_13_qn, d_ff_14_qn, d_ff_15_qn, d_ff_16_qn;

  D_Flip_Flop d_ff_1 (.D(d_ff_1_qn), .clk(Clock), .Q(Count[0]), .Qn(d_ff_1_qn), .reset(Clear));  // open: preset
  D_Flip_Flop d_ff_2 (.D(d_ff_2_qn), .clk(d_ff_15_qn), .Q(Count[8]), .Qn(d_ff_2_qn), .reset(Clear));  // open: preset
  D_Flip_Flop d_ff_3 (.D(d_ff_3_qn), .clk(d_ff_1_qn), .Q(Count[1]), .Qn(d_ff_3_qn), .reset(Clear));  // open: preset
  D_Flip_Flop d_ff_4 (.D(d_ff_4_qn), .clk(d_ff_2_qn), .Q(Count[9]), .Qn(d_ff_4_qn), .reset(Clear));  // open: preset
  D_Flip_Flop d_ff_5 (.D(d_ff_5_qn), .clk(d_ff_3_qn), .Q(Count[2]), .Qn(d_ff_5_qn), .reset(Clear));  // open: preset
  D_Flip_Flop d_ff_6 (.D(d_ff_6_qn), .clk(d_ff_4_qn), .Q(Count[10]), .Qn(d_ff_6_qn), .reset(Clear));  // open: preset
  D_Flip_Flop d_ff_7 (.D(d_ff_7_qn), .clk(d_ff_5_qn), .Q(Count[3]), .Qn(d_ff_7_qn), .reset(Clear));  // open: preset
  D_Flip_Flop d_ff_8 (.D(d_ff_8_qn), .clk(d_ff_6_qn), .Q(Count[11]), .Qn(d_ff_8_qn), .reset(Clear));  // open: preset
  D_Flip_Flop d_ff_9 (.D(d_ff_9_qn), .clk(d_ff_7_qn), .Q(Count[4]), .Qn(d_ff_9_qn), .reset(Clear));  // open: preset
  D_Flip_Flop d_ff_10 (.D(d_ff_10_qn), .clk(d_ff_8_qn), .Q(Count[12]), .Qn(d_ff_10_qn), .reset(Clear));  // open: preset
  D_Flip_Flop d_ff_11 (.D(d_ff_11_qn), .clk(d_ff_9_qn), .Q(Count[5]), .Qn(d_ff_11_qn), .reset(Clear));  // open: preset
  D_Flip_Flop d_ff_12 (
    .D(d_ff_12_qn), .clk(d_ff_10_qn), .Q(Count[13]), .Qn(d_ff_12_qn), .reset(Clear));  // open: preset
  D_Flip_Flop d_ff_13 (.D(d_ff_13_qn), .clk(d_ff_11_qn), .Q(Count[6]), .Qn(d_ff_13_qn), .reset(Clear));  // open: preset
  D_Flip_Flop d_ff_14 (
    .D(d_ff_14_qn), .clk(d_ff_12_qn), .Q(Count[14]), .Qn(d_ff_14_qn), .reset(Clear));  // open: preset
  D_Flip_Flop d_ff_15 (.D(d_ff_15_qn), .clk(d_ff_13_qn), .Q(Count[7]), .Qn(d_ff_15_qn), .reset(Clear));  // open: preset
  D_Flip_Flop d_ff_16 (
    .D(d_ff_16_qn), .clk(d_ff_14_qn), .Q(Count[15]), .Qn(d_ff_16_qn), .reset(Clear));  // open: preset
endmodule

module AutomatedAdder (
  input  [15:0] Addr,
  input  TakeOver,
  input  Write,
  input  [7:0] DataIn,
  input  ResetCount,
  input  ClearSum,
  output [7:0] Sum,
  output [15:0] CountAddr
);

  wire clock_1_out;
  wire [7:0] adder_1_out, DataMem_dout;
  wire [15:0] multiplexer_1_out;

  Clock clock_1 (.out(clock_1_out));
  Multiplexer #(.width(16), .enable("false")) multiplexer_1 (
    .in0(CountAddr), .in1(Addr), .out(multiplexer_1_out), .sel(TakeOver));
  Counter16bit counter16bit_1 (.Clock(clock_1_out), .Clear(ResetCount), .Count(CountAddr));
  RAM #(.addrWidth(16), .trigger("high"), .databus("bibus")) DataMem (
    .addr(multiplexer_1_out), .we(Write), .oe(1'b1), .din(DataIn), .dout(DataMem_dout));
  Adder adder_1 (.a(DataMem_dout), .b(Sum), .out(adder_1_out));  // open: cin, cout
  DTypeFFx8 dtypeffx8_1 (.DataIn(adder_1_out), .Clock(clock_1_out), .Clear(ClearSum), .DataOut(Sum));
endmodule

module AddOrSubtract8bit (
  input  [7:0] Op1,
  input  [7:0] Op2,
  input  Sub,
  output [7:0] Result,
  output Overflow
);

  wire adder_1_cout;
  wire [7:0] xor_1_out;

  xor xor_1 (xor_1_out[0], Op2[0], Sub);
  xor xor_2 (xor_1_out[1], Op2[1], Sub);
  xor xor_3 (xor_1_out[2], Op2[2], Sub);
  xor xor_4 (xor_1_out[3], Op2[3], Sub);
  xor xor_5 (xor_1_out[4], Op2[4], Sub);
  xor xor_6 (xor_1_out[5], Op2[5], Sub);
  xor xor_7 (xor_1_out[6], Op2[6], Sub);
  xor xor_8 (xor_1_out[7], Op2[7], Sub);
  Adder adder_1 (.a(Op1), .b(xor_1_out), .out(Result), .cin(Sub), .cout(adder_1_cout));
  xor xor_9 (Overflow, adder_1_cout, Sub);
endmodule

module AutomatedAddSub (
  input  [15:0] Addr,
  input  TakeOver,
  input  Write,
  input  [7:0] DataIn,
  input  ResetCount,
  input  ClearSum,
  output Overflow,
  output [7:0] Result,
  output [15:0] PC
);

  wire clock_1_out;
  wire [7:0] addorsubtract8bit_1_result, DataMem_dout;
  wire [15:0] multiplexer_1_out;

  Clock clock_1 (.out(clock_1_out));
  Multiplexer #(.width(16), .enable("false")) multiplexer_1 (
    .in0(PC), .in1(Addr), .out(multiplexer_1_out), .sel(TakeOver));
  Counter16bit counter16bit_1 (.Clock(clock_1_out), .Clear(ResetCount), .Count(PC));
  RAM #(.addrWidth(16), .trigger("high"), .databus("bibus")) DataMem (
    .addr(multiplexer_1_out), .we(Write), .oe(1'b1), .din(DataIn), .dout(DataMem_dout));
  DTypeFFx8 dtypeffx8_1 (.DataIn(addorsubtract8bit_1_result), .Clock(clock_1_out), .Clear(ClearSum), .DataOut(Result));
  AddOrSubtract8bit addorsubtract8bit_1 (
    .Op1(Result), .Op2(DataMem_dout), .Sub(multiplexer_1_out[0]), .Result(addorsubtract8bit_1_result),
    .Overflow(Overflow));
endmodule

module InstructionMemory1 (
  input  [15:0] Addr,
  input  TakeOver,
  input  Write,
  input  [7:0] DataIn,
  input  ResetPC,
  input  ClearResult,
  input  Halt,
  output Overflow,
  output [7:0] Result,
  output [15:0] PC
);

  wire and_1_out, clock_1_out, not_1_out;
  wire [7:0] addorsubtract8bit_1_result, CodeMem_dout, DataMem_dout;
  wire [15:0] multiplexer_1_out;

  Clock clock_1 (.out(clock_1_out));
  not not_1 (not_1_out, Halt);
  and and_1 (and_1_out, clock_1_out, not_1_out);
  Multiplexer #(.width(16), .enable("false")) multiplexer_1 (
    .in0(PC), .in1(Addr), .out(multiplexer_1_out), .sel(TakeOver));
  Counter16bit counter16bit_1 (.Clock(and_1_out), .Clear(ResetPC), .Count(PC));
  RAM #(.addrWidth(16), .trigger("high"), .databus("bibus")) DataMem (
    .addr(multiplexer_1_out), .we(Write), .oe(1'b1), .din(DataIn), .dout(DataMem_dout));
  RAM #(.addrWidth(16), .trigger("high"), .databus("bibus")) CodeMem (
    .addr(multiplexer_1_out), .we(1'b0), .oe(1'b1), .din({8{1'b0}}), .dout(CodeMem_dout));
  DTypeFFx8 dtypeffx8_1 (.DataIn(addorsubtract8bit_1_result), .Clock(and_1_out), .Clear(ClearResult), .DataOut(Result));
  AddOrSubtract8bit addorsubtract8bit_1 (
    .Op1(Result), .Op2(DataMem_dout), .Sub(CodeMem_dout[0]), .Result(addorsubtract8bit_1_result),
    .Overflow(Overflow));

  // Notes on the sheet:
  //   Instructions supported:
  //   Add 20h
  //   Subtract 21h
  //   No control panel for code mem:
  //   just edit data values directly
endmodule

module InstructionMemory2 (
  input  [15:0] Addr,
  input  TakeOver,
  input  Write,
  input  [7:0] DataIn,
  input  ResetPC,
  input  ClearResult,
  output Overflow,
  output [7:0] Result,
  output [15:0] PC
);

  wire and_1_out, and_2_out, and_3_out, and_4_out, and_5_out, and_6_out, clock_1_out, not_1_out, not_2_out,
       not_3_out, not_4_out;
  wire [7:0] addorsubtract8bit_1_result, CodeMem_dout, DataMem_dout;
  wire [15:0] multiplexer_1_out;

  Clock clock_1 (.out(clock_1_out));
  not not_1 (not_1_out, and_6_out);
  and and_1 (and_1_out, clock_1_out, not_1_out);
  Multiplexer #(.width(16), .enable("false")) multiplexer_1 (
    .in0(PC), .in1(Addr), .out(multiplexer_1_out), .sel(TakeOver));
  Counter16bit counter16bit_1 (.Clock(and_1_out), .Clear(ResetPC), .Count(PC));
  RAM #(.addrWidth(16), .trigger("high"), .databus("bibus")) DataMem (
    .addr(multiplexer_1_out), .we(Write), .oe(1'b1), .din(DataIn), .dout(DataMem_dout));
  RAM #(.addrWidth(16), .trigger("high"), .databus("bibus")) CodeMem (
    .addr(multiplexer_1_out), .we(1'b0), .oe(1'b1), .din({8{1'b0}}), .dout(CodeMem_dout));
  DTypeFFx8 dtypeffx8_1 (.DataIn(addorsubtract8bit_1_result), .Clock(and_1_out), .Clear(ClearResult), .DataOut(Result));
  AddOrSubtract8bit addorsubtract8bit_1 (
    .Op1(Result), .Op2(DataMem_dout), .Sub(and_5_out), .Result(addorsubtract8bit_1_result),
    .Overflow(Overflow));
  not not_2 (not_2_out, CodeMem_dout[7]);
  not not_3 (not_3_out, CodeMem_dout[0]);
  not not_4 (not_4_out, CodeMem_dout[0]);
  and and_2 (and_2_out, CodeMem_dout[4], not_2_out, not_3_out);
  and and_3 (and_3_out, CodeMem_dout[4], not_2_out, CodeMem_dout[0]);
  and and_4 (and_4_out, CodeMem_dout[5], not_2_out, not_4_out);
  and and_5 (and_5_out, CodeMem_dout[5], not_2_out, CodeMem_dout[0]);
  and and_6 (and_6_out, CodeMem_dout[0], CodeMem_dout[1], CodeMem_dout[2], CodeMem_dout[3], CodeMem_dout[5], CodeMem_dout[6], CodeMem_dout[7]);

  // Notes on the sheet:
  //   Instructions supported:
  //   Add 20h
  //   Subtract 21h
  //   Halt FFh
  //   No control panel for code mem:
  //   just edit data values directly
  //   Control unit
  //   Load
  //   Store
  //   Add
  //   Sub
  //   Halt
endmodule

module InstructionMemory3 (
  input  [15:0] Addr,
  input  TakeOver,
  input  Write,
  input  [7:0] DataIn,
  input  ResetPC,
  input  ClearResult,
  output Overflow,
  output [7:0] Result,
  output [15:0] out_9
);

  wire and_1_out, and_2_out, and_3_out, and_4_out, and_5_out, and_6_out, clock_1_out, not_1_out, not_2_out,
       not_3_out, not_4_out;
  wire [7:0] addorsubtract8bit_1_result, CodeMem_dout, DataMem_dout, multiplexer_2_out;
  wire [15:0] multiplexer_1_out;

  Clock clock_1 (.out(clock_1_out));
  not not_1 (not_1_out, and_6_out);
  and and_1 (and_1_out, clock_1_out, not_1_out);
  Multiplexer #(.width(16), .enable("false")) multiplexer_1 (
    .in0(out_9), .in1(Addr), .out(multiplexer_1_out), .sel(TakeOver));
  Counter16bit counter16bit_1 (.Clock(and_1_out), .Clear(ResetPC), .Count(out_9));
  RAM #(.addrWidth(16), .trigger("high"), .databus("bibus")) DataMem (
    .addr(multiplexer_1_out), .we(Write), .oe(1'b1), .din(DataIn), .dout(DataMem_dout));
  Multiplexer #(.width(8), .enable("false")) multiplexer_2 (
    .in0(addorsubtract8bit_1_result), .in1(DataMem_dout), .out(multiplexer_2_out), .sel(and_2_out));
  RAM #(.addrWidth(16), .trigger("high"), .databus("bibus")) CodeMem (
    .addr(multiplexer_1_out), .we(1'b0), .oe(1'b1), .din({8{1'b0}}), .dout(CodeMem_dout));
  DTypeFFx8 dtypeffx8_1 (.DataIn(multiplexer_2_out), .Clock(and_1_out), .Clear(ClearResult), .DataOut(Result));
  AddOrSubtract8bit addorsubtract8bit_1 (
    .Op1(Result), .Op2(DataMem_dout), .Sub(and_5_out), .Result(addorsubtract8bit_1_result),
    .Overflow(Overflow));
  not not_2 (not_2_out, CodeMem_dout[7]);
  not not_3 (not_3_out, CodeMem_dout[0]);
  not not_4 (not_4_out, CodeMem_dout[0]);
  and and_2 (and_2_out, CodeMem_dout[4], not_2_out, not_3_out);
  and and_3 (and_3_out, CodeMem_dout[4], not_2_out, CodeMem_dout[0]);
  and and_4 (and_4_out, CodeMem_dout[5], not_2_out, not_4_out);
  and and_5 (and_5_out, CodeMem_dout[5], not_2_out, CodeMem_dout[0]);
  and and_6 (and_6_out, CodeMem_dout[0], CodeMem_dout[1], CodeMem_dout[2], CodeMem_dout[3], CodeMem_dout[5], CodeMem_dout[6], CodeMem_dout[7]);

  // Notes on the sheet:
  //   Instructions supported:
  //   Add 20h
  //   Subtract 21h
  //   Load 10h
  //   Halt FFh
  //   No control panel for code mem:
  //   just edit data values directly
  //   Control unit
  //   Load
  //   Store
  //   Add
  //   Sub
  //   Halt
endmodule

module InstructionMemory4 (
  input  [15:0] Addr,
  input  TakeOver,
  input  Write,
  input  [7:0] DataIn,
  input  ResetPC,
  input  ClearResult,
  output Overflow,
  output [7:0] Result,
  output [15:0] PC
);

  wire and_1_out, and_2_out, and_3_out, and_4_out, and_5_out, and_6_out, and_7_out, and_8_out, clock_1_out,
       multiplexer_3_out, not_1_out, not_2_out, not_3_out, not_4_out, not_5_out, not_6_out;
  wire [7:0] addorsubtract8bit_1_result, CodeMem_dout, DataMem_dout, multiplexer_2_out, multiplexer_4_out;
  wire [15:0] multiplexer_1_out;

  Clock clock_1 (.out(clock_1_out));
  not not_1 (not_1_out, and_8_out);
  and and_1 (and_1_out, clock_1_out, not_1_out);
  not not_2 (not_2_out, and_1_out);
  Multiplexer #(.width(16), .enable("false")) multiplexer_1 (
    .in0(PC), .in1(Addr), .out(multiplexer_1_out), .sel(TakeOver));
  Multiplexer #(.width(8), .enable("false")) multiplexer_2 (
    .in0(Result), .in1(DataIn), .out(multiplexer_2_out), .sel(TakeOver));
  Counter16bit counter16bit_1 (.Clock(and_1_out), .Clear(ResetPC), .Count(PC));
  Multiplexer #(.enable("false")) multiplexer_3 (.in0(and_2_out), .in1(Write), .out(multiplexer_3_out), .sel(TakeOver));
  and and_2 (and_2_out, not_2_out, and_5_out);
  RAM #(.addrWidth(16), .trigger("high"), .databus("bibus")) DataMem (
    .addr(multiplexer_1_out), .we(multiplexer_3_out), .oe(1'b1), .din(multiplexer_2_out), .dout(DataMem_dout));
  not not_3 (not_3_out, and_5_out);
  and and_3 (and_3_out, and_1_out, not_3_out);
  Multiplexer #(.width(8), .enable("false")) multiplexer_4 (
    .in0(addorsubtract8bit_1_result), .in1(DataMem_dout), .out(multiplexer_4_out), .sel(and_4_out));
  RAM #(.addrWidth(16), .trigger("high"), .databus("bibus")) CodeMem (
    .addr(multiplexer_1_out), .we(1'b0), .oe(1'b1), .din({8{1'b0}}), .dout(CodeMem_dout));
  DTypeFFx8 dtypeffx8_1 (.DataIn(multiplexer_4_out), .Clock(and_3_out), .Clear(ClearResult), .DataOut(Result));
  AddOrSubtract8bit addorsubtract8bit_1 (
    .Op1(Result), .Op2(DataMem_dout), .Sub(and_7_out), .Result(addorsubtract8bit_1_result),
    .Overflow(Overflow));
  not not_4 (not_4_out, CodeMem_dout[7]);
  not not_5 (not_5_out, CodeMem_dout[0]);
  not not_6 (not_6_out, CodeMem_dout[0]);
  and and_4 (and_4_out, CodeMem_dout[4], not_4_out, not_5_out);
  and and_5 (and_5_out, CodeMem_dout[4], not_4_out, CodeMem_dout[0]);
  and and_6 (and_6_out, CodeMem_dout[5], not_4_out, not_6_out);
  and and_7 (and_7_out, CodeMem_dout[5], not_4_out, CodeMem_dout[0]);
  and and_8 (and_8_out, CodeMem_dout[0], CodeMem_dout[1], CodeMem_dout[2], CodeMem_dout[3], CodeMem_dout[5], CodeMem_dout[6], CodeMem_dout[7]);

  // Notes on the sheet:
  //   for the data RAM
  //   There is some slightly janky stuff
  //   going on here with the write enable
  //   Instructions supported:
  //   Add 20h
  //   Subtract 21h
  //   Load 10h
  //   Store 11h
  //   Halt FFh
  //   No control panel for code mem:
  //   just edit data values directly
  //   Control unit
  //   Load
  //   Store
  //   Add
  //   Sub
  //   Halt
endmodule
