// Logisim project demoMemory.circ as structural Verilog
module NorSRLatch (
  input  S,
  input  R,
  output NotQ,
  output Q
);

  nor nor_1 (NotQ, S, Q);
  nor nor_2 (Q, NotQ, R);
endmodule

module NorDLatch (
  input  D,
  input  Clock,
  output NotQ,
  output Q
);

  wire and_1_out, and_2_out, not_1_out;

  not not_1 (not_1_out, D);
  and and_1 (and_1_out, D, Clock);
  and and_2 (and_2_out, Clock, not_1_out);
  nor nor_1 (NotQ, and_1_out, Q);
  nor nor_2 (Q, NotQ, and_2_out);
endmodule

module NorDLatchx8 (
  input  [7:0] DataIn,
  input  Clock,
  output [7:0] DataOut
);

  NorDLatch nordlatch_1 (.D(DataIn[0]), .Clock(Clock), .Q(DataOut[0]));  // open: NotQ
  NorDLatch nordlatch_2 (.D(DataIn[1]), .Clock(Clock), .Q(DataOut[1]));  // open: NotQ
  NorDLatch nordlatch_3 (.D(DataIn[2]), .Clock(Clock), .Q(DataOut[2]));  // open: NotQ
  NorDLatch nordlatch_4 (.D(DataIn[3]), .Clock(Clock), .Q(DataOut[3]));  // open: NotQ
  NorDLatch nordlatch_5 (.D(DataIn[4]), .Clock(Clock), .Q(DataOut[4]));  // open: NotQ
  NorDLatch nordlatch_6 (.D(DataIn[5]), .Clock(Clock), .Q(DataOut[5]));  // open: NotQ
  NorDLatch nordlatch_7 (.D(DataIn[6]), .Clock(Clock), .Q(DataOut[6]));  // open: NotQ
  NorDLatch nordlatch_8 (.D(DataIn[7]), .Clock(Clock), .Q(DataOut[7]));  // open: NotQ
endmodule

module AdderV1 (
  input  Clock,
  output [7:0] LatchOut
);

  NorDLatchx8 nordlatchx8_1 (.DataIn({8{1'b0}}), .Clock(Clock), .DataOut(LatchOut));
endmodule

module AdderV2 (
  input  Clear,
  input  Clock,
  input  [7:0] DataIn
);

  wire [7:0] adder_1_out, multiplexer_1_out, nordlatchx8_1_dataout;

  Multiplexer #(.width(8), .enable("false")) multiplexer_1 (
    .in0(adder_1_out), .in1({8{1'b0}}), .out(multiplexer_1_out), .sel(Clear));
  NorDLatchx8 nordlatchx8_1 (.DataIn(multiplexer_1_out), .Clock(Clock), .DataOut(nordlatchx8_1_dataout));
  Adder adder_1 (.a(nordlatchx8_1_dataout), .b(DataIn), .out(adder_1_out), .cin(1'b0));  // open: cout

  // Notes on the sheet:
  //   This doesn't actually work :-(
endmodule

module AdderV3 (
  input  Clear,
  input  Clock,
  input  Clock2,
  input  [7:0] DataIn,
  output [7:0] Sum,
  output [7:0] Latch1Out,
  output [7:0] Accumulator
);

  wire [7:0] multiplexer_1_out;

  Multiplexer #(.width(8), .enable("false")) multiplexer_1 (
    .in0(Sum), .in1({8{1'b0}}), .out(multiplexer_1_out), .sel(Clear));
  NorDLatchx8 nordlatchx8_1 (.DataIn(multiplexer_1_out), .Clock(Clock), .DataOut(Latch1Out));
  NorDLatchx8 nordlatchx8_2 (.DataIn(Latch1Out), .Clock(Clock2), .DataOut(Accumulator));
  Adder adder_1 (.a(Accumulator), .b(DataIn), .out(Sum), .cin(1'b0));  // open: cout

  // Notes on the sheet:
  //   This works but is a bit awkward to use
  //   Accumulator
endmodule

module AdderV4 (
  input  Clear,
  input  Clock,
  input  [7:0] DataIn,
  output [7:0] Sum,
  output [7:0] Latch1Out,
  output [7:0] Accumulator
);

  wire not_1_out;
  wire [7:0] multiplexer_1_out;

  Multiplexer #(.width(8), .enable("false")) multiplexer_1 (
    .in0(Sum), .in1({8{1'b0}}), .out(multiplexer_1_out), .sel(Clear));
  not not_1 (not_1_out, Clock);
  NorDLatchx8 nordlatchx8_1 (.DataIn(multiplexer_1_out), .Clock(Clock), .DataOut(Latch1Out));
  NorDLatchx8 nordlatchx8_2 (.DataIn(Latch1Out), .Clock(not_1_out), .DataOut(Accumulator));
  Adder adder_1 (.a(Accumulator), .b(DataIn), .out(Sum), .cin(1'b0));  // open: cout

  // Notes on the sheet:
  //   Now a single clock signal drives the latches, easier to use
  //   Accumulator
endmodule

module NorDFlipFlop (
  input  DataIn,
  input  Clock,
  output NotQ,
  output Q
);

  wire nordlatch_1_q, not_1_out;

  not not_1 (not_1_out, Clock);
  NorDLatch nordlatch_1 (.D(DataIn), .Clock(not_1_out), .Q(nordlatch_1_q));  // open: NotQ
  NorDLatch nordlatch_2 (.D(nordlatch_1_q), .Clock(Clock), .NotQ(NotQ), .Q(Q));
endmodule

module OneBitCounter (
  input  in_1,
  output FFOut
);

  wire clk_out, multiplexer_1_out, nordflipflop_1_notq;

  Clock #(.highDuration(4), .lowDuration(4)) clk (.out(clk_out));
  Clock sysclk ();  // open: out
  Multiplexer #(.enable("false")) multiplexer_1 (
    .in0(nordflipflop_1_notq), .in1(1'b0), .out(multiplexer_1_out), .sel(in_1));
  NorDFlipFlop nordflipflop_1 (.DataIn(multiplexer_1_out), .Clock(clk_out), .NotQ(nordflipflop_1_notq), .Q(FFOut));
endmodule

module OneBitCounterBetter (
  output FFOut
);

  wire clk_out, d_ff_1_qn;

  Clock #(.highDuration(2), .lowDuration(2)) clk (.out(clk_out));
  Clock sysclk ();  // open: out
  D_Flip_Flop d_ff_1 (.D(d_ff_1_qn), .clk(clk_out), .Q(FFOut), .Qn(d_ff_1_qn));  // open: preset, reset
endmodule

module FourBitCounter (
  output Out0,
  output Out1,
  output Out2,
  output Out3
);

  wire clk_out, d_ff_1_qn, d_ff_2_qn, d_ff_3_qn, d_ff_4_qn;

  D_Flip_Flop d_ff_1 (.D(d_ff_1_qn), .clk(clk_out), .Q(Out0), .Qn(d_ff_1_qn));  // open: preset, reset
  Clock #(.highDuration(2), .lowDuration(2)) clk (.out(clk_out));
  Clock sysclk ();  // open: out
  D_Flip_Flop d_ff_2 (.D(d_ff_2_qn), .clk(d_ff_1_qn), .Q(Out1), .Qn(d_ff_2_qn));  // open: preset, reset
  D_Flip_Flop d_ff_3 (.D(d_ff_3_qn), .clk(d_ff_2_qn), .Q(Out2), .Qn(d_ff_3_qn));  // open: preset, reset
  D_Flip_Flop d_ff_4 (.D(d_ff_4_qn), .clk(d_ff_3_qn), .Q(Out3), .Qn(d_ff_4_qn));  // open: preset, reset
endmodule

module FourBitCounterBinary (
  output [3:0] Count
);

  wire clk_out, d_ff_1_qn, d_ff_2_qn, d_ff_3_qn, d_ff_4_qn;

  Clock #(.highDuration(2), .lowDuration(2)) clk (.out(clk_out));
  D_Flip_Flop d_ff_1 (.D(d_ff_1_qn), .clk(clk_out), .Q(Count[0]), .Qn(d_ff_1_qn));  // open: preset, reset
  Clock sysclk ();  // open: out
  D_Flip_Flop d_ff_2 (.D(d_ff_2_qn), .clk(d_ff_1_qn), .Q(Count[1]), .Qn(d_ff_2_qn));  // open: preset, reset
  D_Flip_Flop d_ff_3 (.D(d_ff_3_qn), .clk(d_ff_2_qn), .Q(Count[2]), .Qn(d_ff_3_qn));  // open: preset, reset
  D_Flip_Flop d_ff_4 (.D(d_ff_4_qn), .clk(d_ff_3_qn), .Q(Count[3]), .Qn(d_ff_4_qn));  // open: preset, reset
endmodule

module RAM8bit8in1out (
  input  [7:0] DataIn,
  input  Write,
  input  [2:0] Address,
  output DataOut
);

  wire [7:0] nordlatchx8_1_dataout;

  NorDLatchx8 nordlatchx8_1 (.DataIn(DataIn), .Clock(Write), .DataOut(nordlatchx8_1_dataout));
  Mux8to1 mux8to1_1 (
    .D0(nordlatchx8_1_dataout[0]), .D1(nordlatchx8_1_dataout[1]), .D2(nordlatchx8_1_dataout[2]),
    .D3(nordlatchx8_1_dataout[3]), .D4(nordlatchx8_1_dataout[4]), .D5(nordlatchx8_1_dataout[5]),
    .D6(nordlatchx8_1_dataout[6]), .D7(nordlatchx8_1_dataout[7]), .A0(Address[0]), .A1(Address[1]),
    .A2(Address[2]), .Q(DataOut));
endmodule

module Mux8to1 (
  input  D0,
  input  D1,
  input  D2,
  input  D3,
  input  D4,
  input  D5,
  input  D6,
  input  D7,
  input  A0,
  input  A1,
  input  A2,
  output Q
);

  wire and_1_out, and_2_out, and_3_out, and_4_out, and_5_out, and_6_out, and_7_out, and_8_out, not_1_out,
       not_2_out, not_3_out;

  not not_1 (not_1_out, A0);
  not not_2 (not_2_out, A1);
  not not_3 (not_3_out, A2);
  and and_1 (and_1_out, D0, not_1_out, not_2_out, not_3_out);
  and and_2 (and_2_out, D1, A0, not_2_out, not_3_out);
  and and_3 (and_3_out, D2, not_1_out, A1, not_3_out);
  and and_4 (and_4_out, D3, A0, A1, not_3_out);
  and and_5 (and_5_out, D4, not_1_out, not_2_out, A2);
  and and_6 (and_6_out, D5, A0, not_2_out, A2);
  and and_7 (and_7_out, D6, not_1_out, A1, A2);
  and and_8 (and_8_out, D7, A0, A1, A2);
  or or_1 (Q, and_1_out, and_2_out, and_3_out, and_4_out, and_5_out, and_6_out, and_7_out, and_8_out);
endmodule

module Demux1to8 (
  input  DataIn,
  input  A0,
  input  A1,
  input  A2,
  output W0,
  output W1,
  output W2,
  output W3,
  output W4,
  output W5,
  output W6,
  output W7
);

  wire not_1_out, not_2_out, not_3_out;

  not not_1 (not_1_out, A0);
  not not_2 (not_2_out, A1);
  not not_3 (not_3_out, A2);
  and and_1 (W0, DataIn, not_1_out, not_2_out, not_3_out);
  and and_2 (W1, DataIn, A0, not_2_out, not_3_out);
  and and_3 (W2, DataIn, not_1_out, A1, not_3_out);
  and and_4 (W3, DataIn, A0, A1, not_3_out);
  and and_5 (W4, DataIn, not_1_out, not_2_out, A2);
  and and_6 (W5, DataIn, A0, not_2_out, A2);
  and and_7 (W6, DataIn, not_1_out, A1, A2);
  and and_8 (W7, DataIn, A0, A1, A2);
endmodule

module RAM8bit1in1out (
  input  DataIn,
  input  Write,
  input  [2:0] Address,
  output DataOut
);

  wire demux1to8_1_w0, demux1to8_1_w1, demux1to8_1_w2, demux1to8_1_w3, demux1to8_1_w4, demux1to8_1_w5,
       demux1to8_1_w6, demux1to8_1_w7, nordlatch_1_q, nordlatch_2_q, nordlatch_3_q, nordlatch_4_q,
       nordlatch_5_q, nordlatch_6_q, nordlatch_7_q, nordlatch_8_q;

  Demux1to8 demux1to8_1 (
    .DataIn(Write), .A0(Address[0]), .A1(Address[1]), .A2(Address[2]), .W0(demux1to8_1_w0),
    .W1(demux1to8_1_w1), .W2(demux1to8_1_w2), .W3(demux1to8_1_w3), .W4(demux1to8_1_w4), .W5(demux1to8_1_w5),
    .W6(demux1to8_1_w6), .W7(demux1to8_1_w7));
  NorDLatch nordlatch_1 (.D(DataIn), .Clock(demux1to8_1_w0), .Q(nordlatch_1_q));  // open: NotQ
  NorDLatch nordlatch_2 (.D(DataIn), .Clock(demux1to8_1_w1), .Q(nordlatch_2_q));  // open: NotQ
  NorDLatch nordlatch_3 (.D(DataIn), .Clock(demux1to8_1_w2), .Q(nordlatch_3_q));  // open: NotQ
  NorDLatch nordlatch_4 (.D(DataIn), .Clock(demux1to8_1_w3), .Q(nordlatch_4_q));  // open: NotQ
  NorDLatch nordlatch_5 (.D(DataIn), .Clock(demux1to8_1_w4), .Q(nordlatch_5_q));  // open: NotQ
  NorDLatch nordlatch_6 (.D(DataIn), .Clock(demux1to8_1_w5), .Q(nordlatch_6_q));  // open: NotQ
  NorDLatch nordlatch_7 (.D(DataIn), .Clock(demux1to8_1_w6), .Q(nordlatch_7_q));  // open: NotQ
  NorDLatch nordlatch_8 (.D(DataIn), .Clock(demux1to8_1_w7), .Q(nordlatch_8_q));  // open: NotQ
  Mux8to1 mux8to1_1 (
    .D0(nordlatch_1_q), .D1(nordlatch_2_q), .D2(nordlatch_3_q), .D3(nordlatch_4_q), .D4(nordlatch_5_q),
    .D5(nordlatch_6_q), .D6(nordlatch_7_q), .D7(nordlatch_8_q), .A0(Address[0]), .A1(Address[1]),
    .A2(Address[2]), .Q(DataOut));
endmodule

module RAM8bit1in1outBetter (
  input  DataIn,
  input  Write,
  input  [2:0] Address,
  output DataOut
);

  wire d_ff_1_q, d_ff_2_q, d_ff_3_q, d_ff_4_q, d_ff_5_q, d_ff_6_q, d_ff_7_q, d_ff_8_q, demux1to8_1_w0,
       demux1to8_1_w1, demux1to8_1_w2, demux1to8_1_w3, demux1to8_1_w4, demux1to8_1_w5, demux1to8_1_w6,
       demux1to8_1_w7;

  Demux1to8 demux1to8_1 (
    .DataIn(Write), .A0(Address[0]), .A1(Address[1]), .A2(Address[2]), .W0(demux1to8_1_w0),
    .W1(demux1to8_1_w1), .W2(demux1to8_1_w2), .W3(demux1to8_1_w3), .W4(demux1to8_1_w4), .W5(demux1to8_1_w5),
    .W6(demux1to8_1_w6), .W7(demux1to8_1_w7));
  D_Flip_Flop #(.trigger("high")) d_ff_1 (.D(DataIn), .clk(demux1to8_1_w0), .Q(d_ff_1_q));  // open: Qn, preset, reset
  D_Flip_Flop #(.trigger("high")) d_ff_2 (.D(DataIn), .clk(demux1to8_1_w1), .Q(d_ff_2_q));  // open: Qn, preset, reset
  D_Flip_Flop #(.trigger("high")) d_ff_3 (.D(DataIn), .clk(demux1to8_1_w2), .Q(d_ff_3_q));  // open: Qn, preset, reset
  D_Flip_Flop #(.trigger("high")) d_ff_4 (.D(DataIn), .clk(demux1to8_1_w3), .Q(d_ff_4_q));  // open: Qn, preset, reset
  D_Flip_Flop #(.trigger("high")) d_ff_5 (.D(DataIn), .clk(demux1to8_1_w4), .Q(d_ff_5_q));  // open: Qn, preset, reset
  D_Flip_Flop #(.trigger("high")) d_ff_6 (.D(DataIn), .clk(demux1to8_1_w5), .Q(d_ff_6_q));  // open: Qn, preset, reset
  D_Flip_Flop #(.trigger("high")) d_ff_7 (.D(DataIn), .clk(demux1to8_1_w6), .Q(d_ff_7_q));  // open: Qn, preset, reset
  D_Flip_Flop #(.trigger("high")) d_ff_8 (.D(DataIn), .clk(demux1to8_1_w7), .Q(d_ff_8_q));  // open: Qn, preset, reset
  Mux8to1 mux8to1_1 (
    .D0(d_ff_1_q), .D1(d_ff_2_q), .D2(d_ff_3_q), .D3(d_ff_4_q), .D4(d_ff_5_q), .D5(d_ff_6_q), .D6(d_ff_7_q),
    .D7(d_ff_8_q), .A0(Address[0]), .A1(Address[1]), .A2(Address[2]), .Q(DataOut));
endmodule

module Ram8x2 (
  input  [1:0] DataIn,
  input  Write,
  input  [2:0] Address,
  output [1:0] DataOut
);

  RAM8bit1in1outBetter ram8bit1in1outbetter_1 (
    .DataIn(DataIn[0]), .Write(Write), .Address(Address), .DataOut(DataOut[0]));
  RAM8bit1in1outBetter ram8bit1in1outbetter_2 (
    .DataIn(DataIn[1]), .Write(Write), .Address(Address), .DataOut(DataOut[1]));
endmodule
