// Logisim project demoSequentialLogic.circ as structural Verilog
module NorSRLatch (
  input  S,
  input  R,
  output NotQ,
  output Q
);

  nor nor_1 (NotQ, S, Q);
  nor nor_2 (Q, NotQ, R);
endmodule

module NorDLatch (
  input  D,
  input  Clock,
  output NotQ,
  output Q
);

  wire and_1_out, and_2_out, not_1_out;

  not not_1 (not_1_out, D);
  and and_1 (and_1_out, D, Clock);
  and and_2 (and_2_out, Clock, not_1_out);
  nor nor_1 (NotQ, and_1_out, Q);
  nor nor_2 (Q, NotQ, and_2_out);
endmodule

module NorDLatchx8 (
  input  [7:0] DataIn,
  input  Clock,
  output [7:0] DataOut
);

  NorDLatch nordlatch_1 (.D(DataIn[0]), .Clock(Clock), .Q(DataOut[0]));  // open: NotQ
  NorDLatch nordlatch_2 (.D(DataIn[1]), .Clock(Clock), .Q(DataOut[1]));  // open: NotQ
  NorDLatch nordlatch_3 (.D(DataIn[2]), .Clock(Clock), .Q(DataOut[2]));  // open: NotQ
  NorDLatch nordlatch_4 (.D(DataIn[3]), .Clock(Clock), .Q(DataOut[3]));  // open: NotQ
  NorDLatch nordlatch_5 (.D(DataIn[4]), .Clock(Clock), .Q(DataOut[4]));  // open: NotQ
  NorDLatch nordlatch_6 (.D(DataIn[5]), .Clock(Clock), .Q(DataOut[5]));  // open: NotQ
  NorDLatch nordlatch_7 (.D(DataIn[6]), .Clock(Clock), .Q(DataOut[6]));  // open: NotQ
  NorDLatch nordlatch_8 (.D(DataIn[7]), .Clock(Clock), .Q(DataOut[7]));  // open: NotQ
endmodule

module AdderV1 (
  input  Clock,
  output [7:0] LatchOut
);

  NorDLatchx8 nordlatchx8_1 (.DataIn({8{1'b0}}), .Clock(Clock), .DataOut(LatchOut));
endmodule

module AdderV2 (
  input  Clear,
  input  Clock,
  input  [7:0] DataIn
);

  wire [7:0] adder_1_out, multiplexer_1_out, nordlatchx8_1_dataout;

  Multiplexer #(.width(8), .enable("false")) multiplexer_1 (
    .in0(adder_1_out), .in1({8{1'b0}}), .out(multiplexer_1_out), .sel(Clear));
  NorDLatchx8 nordlatchx8_1 (.DataIn(multiplexer_1_out), .Clock(Clock), .DataOut(nordlatchx8_1_dataout));
  Adder adder_1 (.a(nordlatchx8_1_dataout), .b(DataIn), .out(adder_1_out), .cin(1'b0));  // open: cout

  // Notes on the sheet:
  //   This doesn't actually work :-(
endmodule

module AdderV3 (
  input  Clear,
  input  Clock,
  input  Clock2,
  input  [7:0] DataIn,
  output [7:0] Sum,
  output [7:0] Latch1Out,
  output [7:0] Accumulator
);

  wire [7:0] multiplexer_1_out;

  Multiplexer #(.width(8), .enable("false")) multiplexer_1 (
    .in0(Sum), .in1({8{1'b0}}), .out(multiplexer_1_out), .sel(Clear));
  NorDLatchx8 nordlatchx8_1 (.DataIn(multiplexer_1_out), .Clock(Clock), .DataOut(Latch1Out));
  NorDLatchx8 nordlatchx8_2 (.DataIn(Latch1Out), .Clock(Clock2), .DataOut(Accumulator));
  Adder adder_1 (.a(Accumulator), .b(DataIn), .out(Sum), .cin(1'b0));  // open: cout

  // Notes on the sheet:
  //   This works but is a bit awkward to use
  //   Accumulator
endmodule

module AdderV4 (
  input  Clear,
  input  Clock,
  input  [7:0] DataIn,
  output [7:0] Sum,
  output [7:0] Latch1Out,
  output [7:0] Accumulator
);

  wire not_1_out;
  wire [7:0] multiplexer_1_out;

  Multiplexer #(.width(8), .enable("false")) multiplexer_1 (
    .in0(Sum), .in1({8{1'b0}}), .out(multiplexer_1_out), .sel(Clear));
  not not_1 (not_1_out, Clock);
  NorDLatchx8 nordlatchx8_1 (.DataIn(multiplexer_1_out), .Clock(Clock), .DataOut(Latch1Out));
  NorDLatchx8 nordlatchx8_2 (.DataIn(Latch1Out), .Clock(not_1_out), .DataOut(Accumulator));
  Adder adder_1 (.a(Accumulator), .b(DataIn), .out(Sum), .cin(1'b0));  // open: cout

  // Notes on the sheet:
  //   Now a single clock signal drives the latches, easier to use
  //   Accumulator
endmodule

module NorDFlipFlop (
  input  DataIn,
  input  Clock,
  output NotQ,
  output Q
);

  wire nordlatch_1_q, not_1_out;

  not not_1 (not_1_out, Clock);
  NorDLatch nordlatch_1 (.D(DataIn), .Clock(not_1_out), .Q(nordlatch_1_q));  // open: NotQ
  NorDLatch nordlatch_2 (.D(nordlatch_1_q), .Clock(Clock), .NotQ(NotQ), .Q(Q));
endmodule

module OneBitCounter (
  input  in_1,
  output FFOut
);

  wire clk_out, multiplexer_1_out, nordflipflop_1_notq;

  Clock #(.highDuration(4), .lowDuration(4)) clk (.out(clk_out));
  Clock sysclk ();  // open: out
  Multiplexer #(.enable("false")) multiplexer_1 (
    .in0(nordflipflop_1_notq), .in1(1'b0), .out(multiplexer_1_out), .sel(in_1));
  NorDFlipFlop nordflipflop_1 (.DataIn(multiplexer_1_out), .Clock(clk_out), .NotQ(nordflipflop_1_notq), .Q(FFOut));
endmodule

module OneBitCounterBetter (
  output FFOut
);

  wire clk_out, d_ff_1_qn;

  Clock #(.highDuration(2), .lowDuration(2)) clk (.out(clk_out));
  Clock sysclk ();  // open: out
  D_Flip_Flop d_ff_1 (.D(d_ff_1_qn), .clk(clk_out), .Q(FFOut), .Qn(d_ff_1_qn));  // open: preset, reset
endmodule

module FourBitCounter (
  output Out0,
  output Out1,
  output Out2,
  output Out3
);

  wire clk_out, d_ff_1_qn, d_ff_2_qn, d_ff_3_qn, d_ff_4_qn;

  D_Flip_Flop d_ff_1 (.D(d_ff_1_qn), .clk(clk_out), .Q(Out0), .Qn(d_ff_1_qn));  // open: preset, reset
  Clock #(.highDuration(2), .lowDuration(2)) clk (.out(clk_out));
  Clock sysclk ();  // open: out
  D_Flip_Flop d_ff_2 (.D(d_ff_2_qn), .clk(d_ff_1_qn), .Q(Out1), .Qn(d_ff_2_qn));  // open: preset, reset
  D_Flip_Flop d_ff_3 (.D(d_ff_3_qn), .clk(d_ff_2_qn), .Q(Out2), .Qn(d_ff_3_qn));  // open: preset, reset
  D_Flip_Flop d_ff_4 (.D(d_ff_4_qn), .clk(d_ff_3_qn), .Q(Out3), .Qn(d_ff_4_qn));  // open: preset, reset
endmodule

module FourBitCounterBinary (
  output [3:0] Count
);

  wire clk_out, d_ff_1_qn, d_ff_2_qn, d_ff_3_qn, d_ff_4_qn;

  Clock #(.highDuration(2), .lowDuration(2)) clk (.out(clk_out));
  D_Flip_Flop d_ff_1 (.D(d_ff_1_qn), .clk(clk_out), .Q(Count[0]), .Qn(d_ff_1_qn));  // open: preset, reset
  Clock sysclk ();  // open: out
  D_Flip_Flop d_ff_2 (.D(d_ff_2_qn), .clk(d_ff_1_qn), .Q(Count[1]), .Qn(d_ff_2_qn));  // open: preset, reset
  D_Flip_Flop d_ff_3 (.D(d_ff_3_qn), .clk(d_ff_2_qn), .Q(Count[2]), .Qn(d_ff_3_qn));  // open: preset, reset
  D_Flip_Flop d_ff_4 (.D(d_ff_4_qn), .clk(d_ff_3_qn), .Q(Count[3]), .Qn(d_ff_4_qn));  // open: preset, reset
endmodule
